# Fritzing sketch step_00_led (saved by Fritzing 0.9.4)
breadboards: 1

parts:
  U1 = NodeMCU V3.0
  LED1 = LED - 5mm [color="Red (633nm)" package="5 mm [THT]"]  # not connected
  R1 = Resistor [tolerance=±5% resistance=220 package=THT]

nets:
  N1: U1.GND#6, U1.GND#13, U1.GND#16, U1.GND#33, R1.Pin_0

custom parts:
  NodeMCU V3.0: ESP8266 based NodeMCU
