# Fritzing sketch step_30_traffic_light (saved by Fritzing 0.9.4)
breadboards: 1

parts:
  LED1 = smd LED [color="Red (633nm)" package="1206 [SMD]"]  # not connected
  R1 = Resistor [tolerance=±5% resistance=220 package="0805 [SMD]"]
  LED2 = smd LED [color="Yellow (595nm)" package="1206 [SMD]"]  # not connected
  LED3 = smd LED [color="Green (565nm)" package="1206 [SMD]"]  # not connected
  R2 = Resistor [tolerance=±5% resistance=220 package="0805 [SMD]"]
  R3 = Resistor [tolerance=±5% resistance=220 package="0805 [SMD]"]
  U1 = NodeMCU V3.0

nets:
  N1: R1.Pin_0, R2.Pin_0, R3.Pin_0, U1.GND#6, U1.GND#13, U1.GND#16, U1.GND#33

custom parts:
  NodeMCU V3.0: ESP8266 based NodeMCU
