# Fritzing sketch step_40_button_input (saved by Fritzing 0.9.4)
breadboards: 1

parts:
  R1 = Resistor [tolerance=±5% resistance=220 package="0805 [SMD]"]
  S1 = Pushbutton [package="[THT]"]
  LED1 = LED - 5mm [color="Red (633nm)" package="5 mm [THT]"]  # not connected
  U1 = NodeMCU V3.0

nets:
  N1: R1.Pin_0, S1.Pin_3, S1.Pin_4, U1.GND#6, U1.GND#13, U1.GND#16, U1.GND#33
  N2: S1.Pin_1, S1.Pin_2, U1.D3

custom parts:
  NodeMCU V3.0: ESP8266 based NodeMCU
